// Digital circuit processor.dig as structural Verilog
module processor (
  input  clk
);

  wire B_src, PC_src, RAM_r, RAM_w, ula_1_zero, W_reg;
  wire [1:0] ImmC, Resu_src;
  wire [2:0] ULAc;
  wire [4:0] code_memory_d_2;
  wire [15:0] add_1_s, add_2_s, multiplexer_1_out, PC_q;
  wire [31:0] bitextender_1_out, code_memory_d, immediatetransformer_1_output, multiplexer_2_out,
       multiplexer_3_out, ramdualport_1_d, registrador_1_a, registrador_1_b, ula_1_output;

  Multiplexer #(.Bits(16)) multiplexer_1 (.sel(PC_src), .in_0(add_1_s), .in_1(add_2_s), .out(multiplexer_1_out));
  D_FF #(.Bits(16)) PC (.D(multiplexer_1_out), .C(clk), .Q(PC_q));  // open: nQ
  Add #(.Bits(16)) add_1 (.a(16'h4), .b(PC_q), .c_i(1'b0), .s(add_1_s));  // open: c_o
  ROM #(.AddrBits(16), .isProgramMemory("true"), .Bits(32)) code_memory (
    .A(PC_q), .sel(1'b1), .D({code_memory_d[31:12], code_memory_d_2, code_memory_d[6:0]}));
  controlUnit controlunit_1 (
    .A({code_memory_d[31:12], code_memory_d_2, code_memory_d[6:0]}), .zero(ula_1_zero),
    .out({ULAc, PC_src, W_reg, ImmC, B_src, Resu_src, RAM_w, RAM_r}));
  registrador registrador_1 (
    .rs1(code_memory_d[19:15]), .rs2(code_memory_d[24:20]), .rd(code_memory_d_2), .ula(multiplexer_3_out),
    .ck(clk), .W_reg(W_reg), .A(registrador_1_a), .B(registrador_1_b));
  immediateTransformer immediatetransformer_1 (
    .\output (immediatetransformer_1_output), .ImmC(ImmC),
    .in({code_memory_d[31:12], code_memory_d_2, code_memory_d[6:0]}));
  BitExtender #(.inputBits(16), .outputBits(32)) bitextender_1 (.in(add_1_s), .out(bitextender_1_out));
  Multiplexer #(.Bits(32)) multiplexer_2 (
    .sel(B_src), .in_0(registrador_1_b), .in_1(immediatetransformer_1_output), .out(multiplexer_2_out));
  Add #(.Bits(16)) add_2 (.a(PC_q), .b(immediatetransformer_1_output[15:0]), .c_i(1'b0), .s(add_2_s));  // open: c_o
  ula ula_1 (.A(registrador_1_a), .B(multiplexer_2_out), .zero(ula_1_zero), .Output(ula_1_output), .c_ula(ULAc));
  RAMDualPort #(.AddrBits(24), .Bits(32)) ramdualport_1 (
    .A(ula_1_output[23:0]), .Din(registrador_1_b), .str(RAM_w), .C(clk), .ld(RAM_r), .D(ramdualport_1_d));
  Multiplexer #(.Selector_Bits(2), .Bits(32)) multiplexer_3 (
    .sel(Resu_src), .in_0(ula_1_output), .in_1(ramdualport_1_d), .in_2(bitextender_1_out), .in_3({32{1'b0}}),
    .out(multiplexer_3_out));

  // Notes on the sheet:
  //   contents of code_memory (hex, n*v repeats v):
  //   a00493,0,0,0,500913,0,0,0,12489b3,0,0,0,98023
endmodule
